# Fritzing sketch alarm_schema (saved by Fritzing 0.9.3b)
breadboards: 1

parts:
  Součástka1 = Arduino Uno (Rev3)
  Součástka2 = Logic Level Converter
  LED1 = LED - 5mm [color="Red (633nm)" package="5 mm [THT]"]
  LED2 = LED - 5mm [color="Green (570nm)" package="5 mm [THT]"]
  C2 = Electrolytic Capacitor [capacitance=1µF voltage=16V package="1010 [SMD, electrolytic]"]
  Matrix_keypad1 = KEYPAD 4x4
  R1 = Resistor [tolerance=±5% resistance=1k package="0805 [SMD]"]
  R2 = Resistor [tolerance=±5% resistance=1k package="0805 [SMD]"]
  Součástka3 = Breadboard Power Supply Board SMD
  Espessif_Serial_Wifi_Modul_1 = ESP8266 ESP01 [part_number=ESP8266 package=THT]
  R3 = Resistor [tolerance=±5% resistance=4.7k package=THT]
  PIR1 = PIR sensor

nets:
  N1: Součástka1.D8, Matrix_keypad1.col2
  N2: Součástka1.D9_PWM, Matrix_keypad1.col1
  N3: Součástka1.D10_PWM/SS, Součástka2.RX2_HV
  N4: Součástka1.D11_PWM/MOSI, PIR1.SIG
  N5: Součástka1.D12/MISO, Součástka2.TX2_HV
  N6: Součástka1.D2, Matrix_keypad1.row4
  N7: Součástka1.D3_PWM, Matrix_keypad1.row3
  N8: Součástka1.D4, Matrix_keypad1.row2
  N9: Součástka1.D5_PWM, Matrix_keypad1.row1
  N10: Součástka1.D6_PWM, Matrix_keypad1.col4
  N11: Součástka1.D7, Matrix_keypad1.col3
  5V: Součástka1.5V, Součástka2.HV, R1.Pin_1, R2.Pin_1, PIR1.VDD
  GND: Součástka1.GND, Součástka2.GND, LED1.cathode, LED2.cathode, C2.-, Součástka3.GND, Espessif_Serial_Wifi_Modul_1.GND, PIR1.GND
  N12: Součástka2.TX2_LV, Espessif_Serial_Wifi_Modul_1.RXD
  N13: Součástka2.RX2_LV, Espessif_Serial_Wifi_Modul_1.TXD
  VCC: Součástka2.LV, C2.+, Součástka3.VCC, Espessif_Serial_Wifi_Modul_1.VCC, R3.Pin_0
  N14: LED1.anode, R2.Pin_0
  N15: LED2.anode, R1.Pin_0
  N16: Espessif_Serial_Wifi_Modul_1.CH_PD, R3.Pin_1

custom parts:
  KEYPAD 4x4: Matrix keypad 16 buttons, 4 rows x 4 columns
  ESP8266 ESP01: Generic WiFi Module based on the ESP8266 with onboard PCB antenna and UART communications
